# Fritzing sketch hw (saved by Fritzing 0.9.3b)

parts:
  M1 = STM32407VG Discovery
  Part1 = FTDI Basic Programmer

nets:
  N1: M1.PA3, M1.PC3, Part1.TXO
  N2: M1.GND-24, M1.GND-25, Part1.GND
  N3: M1.PA2, Part1.RXI
  N4: M1.3V-72, M1.3V-101, Part1.POWER

custom parts:
  STM32407VG Discovery: The STM32F4DISCOVERY Discovery kit allows users to easily develop applications with the STM32F407VG high performance microcontroller with the ARM® Cortex®-M4 32-bit core. It includes everything required either for beginners or for experienced users to get quickly started.Based on STM32F407VG, it includes an ST-LINK/V2 or ST-LINK/V2-A embedded debug tool, two ST-MEMS digital accelerometers, a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
